// Logisim project cycle fsm.circ as structural Verilog: 1 circuit, main circuit main
module main (
  input  clk,
  input  X,
  output s1,
  output s0
);

  wire and_1_out, and_2_out, and_3_out, and_4_out, S0_q, S1_q;

  D_Flip_Flop u_S1 (.clk(clk), .D(s1), .Q(S1_q));  // open: Qn, preset, en, reset
  D_Flip_Flop u_S0 (.clk(clk), .D(s0), .Q(S0_q), .Qn(s0));  // open: preset, en, reset
  and and_1 (and_1_out, ~X, ~S1_q, ~S0_q);  // AND_Gate
  and and_2 (and_2_out, ~X, S1_q, S0_q);  // AND_Gate
  and and_3 (and_3_out, X, ~S1_q, S0_q);  // AND_Gate
  and and_4 (and_4_out, X, S1_q, ~S0_q);  // AND_Gate
  or or_1 (s1, and_1_out, and_2_out, and_3_out, and_4_out);
endmodule
